// Logisim project MUAZ.circ as structural Verilog: 10 circuits, main circuit main
module main (
);

  wire and_1_out, and_1bit_implementation_1_out_3, and_1bit_implementation_2_out_3,
       and_1bit_implementation_3_out_3, and_1bit_implementation_4_out_3, and_1bit_implementation_5_out_3,
       and_3_out, and_4_out, and_5_out, and_6_out, and_7_out, and_8_out, and_9_out, and_10_out, and_11_out,
       and_12_out, and_13_out, and_14_out, and_15_out, and_16_out, and_17_out, and_18_out, and_19_out,
       and_20_out, and_21_out, and_22_out, and_23_out, and_24_out, and_25_out, and_26_out, and_27_out,
       and_28_out, and_29_out, and_30_out, and_31_out, and_32_out, and_33_out, and_50_out, and_51_out,
       and_52_out, and_53_out, and_54_out, and_55_out, and_56_out, and_57_out, and_58_out, and_59_out,
       and_60_out, and_61_out, and_62_out, and_63_out, and_64_out, and_65_out, and_66_out, and_67_out,
       and_68_out, and_69_out, and_70_out, and_71_out, and_72_out, and_73_out, and_74_out, and_75_out,
       and_76_out, and_77_out, and_78_out, and_79_out, and_80_out, and_81_out, and_98_out, and_99_out,
       and_100_out, and_101_out, and_102_out, and_103_out, and_104_out, and_105_out, and_106_out,
       and_107_out, and_108_out, and_109_out, and_110_out, and_111_out, and_112_out, and_113_out,
       and_114_out, and_115_out, and_116_out, and_117_out, and_118_out, and_119_out, and_120_out,
       and_121_out, and_122_out, and_123_out, and_124_out, and_125_out, and_126_out, and_127_out,
       and_128_out, and_129_out, and_146_out, and_147_out, and_148_out, and_149_out, and_150_out,
       and_151_out, and_152_out, and_153_out, and_154_out, and_155_out, and_156_out, and_157_out,
       and_158_out, and_159_out, and_160_out, and_161_out, and_162_out, and_163_out, and_164_out,
       and_165_out, and_166_out, and_167_out, and_168_out, and_169_out, and_170_out, and_171_out,
       and_172_out, and_173_out, and_174_out, and_175_out, and_176_out, and_177_out, clock_1_out,
       comparator_1_eq, comparator_2_gt, comparator_3_eq, comparator_3_lt, comparator_4_eq, comparator_4_lt,
       comparator_5_lt, comparator_6_lt, decoder_1_out0, decoder_1_out1, decoder_1_out2, decoder_1_out3,
       decoder_1_out4, decoder_1_out5, decoder_1_out6, decoder_1_out7, decoder_2_out4, decoder_2_out5,
       decoder_2_out8, decoder_2_out12, decoder_2_out13, decoder_2_out24, decoder_2_out25, decoder_2_out27,
       multiplexer_2_out, multiplexer_3_out, nor_1_out, not_1_out, or_1bit_3input_implementation_1_out_4,
       or_1bit_3input_implementation_2_p3, or_2input_implementation_1_out_3,
       or_2input_implementation_2_out_3, xor_1bit_2input_implementation_1_out_3,
       xor_1bit_2input_implementation_2_out_3;
  wire [1:0] decoder_2_out0;
  wire [2:0] undriven;
  wire [15:0] register_1_q, register_1_q_2, register_2_q, register_2_q_2, register_3_q, register_3_q_2,
       register_4_q, register_4_q_2, register_5_q, register_5_q_2;
  wire [23:0] and_2_out, bit_extender_1_out, bit_extender_2_out;
  wire [31:0] adder_1_out, adder_2_out, and_32bit_implementation_1_out_3, and_32bit_implementation_2_out_3,
       and_32bit_implementation_3_out_3, and_32bit_implementation_4_out_3, and_32bit_implementation_5_out_3,
       and_32bit_implementation_6_out_3, and_34_out, and_35_out, and_36_out, and_37_out, and_38_out,
       and_39_out, and_40_out, and_41_out, and_42_out, and_43_out, and_44_out, and_45_out, and_46_out,
       and_47_out, and_48_out, and_49_out, and_82_out, and_83_out, and_84_out, and_85_out, and_86_out,
       and_87_out, and_88_out, and_89_out, and_90_out, and_91_out, and_92_out, and_93_out, and_94_out,
       and_95_out, and_96_out, and_97_out, and_130_out, and_131_out, and_132_out, and_133_out, and_134_out,
       and_135_out, and_136_out, and_137_out, and_138_out, and_139_out, and_140_out, and_141_out,
       and_142_out, and_143_out, and_144_out, and_145_out, and_178_out, and_179_out, and_180_out,
       and_181_out, and_182_out, and_183_out, and_184_out, and_185_out, and_186_out, and_187_out,
       and_188_out, and_189_out, and_190_out, and_191_out, and_192_out, and_193_out, bit_extender_3_out,
       bit_extender_4_out, bit_extender_5_out, bit_extender_6_out, bit_extender_7_out, bit_extender_8_out,
       bit_extender_9_out, bit_extender_10_out, bit_extender_11_out, bit_extender_12_out,
       bit_extender_13_out, bit_extender_14_out, bit_extender_15_out, bit_extender_16_out,
       bit_extender_17_out, bit_extender_18_out, bit_extender_19_out, bit_extender_20_out,
       bit_extender_21_out, bit_extender_22_out, bit_extender_23_out, bit_extender_24_out,
       bit_extender_25_out, bit_extender_26_out, bit_extender_27_out, bit_extender_28_out,
       bit_extender_29_out, bit_extender_30_out, bit_extender_31_out, bit_extender_32_out,
       bit_extender_33_out, bit_extender_34_out, bit_extender_35_out, bit_extender_36_out,
       bit_extender_37_out, bit_extender_38_out, bit_extender_39_out, bit_extender_40_out,
       bit_extender_41_out, bit_extender_42_out, bit_extender_43_out, bit_extender_44_out,
       bit_extender_45_out, bit_extender_46_out, bit_extender_47_out, bit_extender_48_out,
       bit_extender_49_out, bit_extender_50_out, bit_extender_51_out, bit_extender_52_out,
       bit_extender_53_out, bit_extender_54_out, bit_extender_55_out, bit_extender_56_out,
       bit_extender_57_out, bit_extender_58_out, bit_extender_59_out, bit_extender_60_out,
       bit_extender_61_out, bit_extender_62_out, bit_extender_63_out, bit_extender_64_out,
       bit_extender_65_out, bit_extender_66_out, bit_extender_67_out, bit_extender_68_out,
       bit_extender_69_out, bit_extender_70_out, bit_extender_71_out, bit_extender_72_out,
       bit_extender_73_out, bit_extender_74_out, bit_extender_75_out, bit_extender_76_out,
       bit_extender_77_out, DMEM_dout, IMEM_dout, multiplexer_1_out, multiplexer_4_out, multiplexer_5_out,
       multiplexer_6_out, multiplexer_7_out, multiplexer_8_out, multiplexer_9_out, multiplexer_10_out,
       multiplexer_11_out, or_1_out, or_2_out, or_3_out, or_4_out, or_5_out, or_6_out, or_7_out, or_8_out,
       or_9_out, or_10_out, or_11_out, or_12_out, or_13_out, or_14_out, or_15_out, or_16_out, or_17_out,
       or_18_out, or_19_out, or_20_out, or_21_out, or_22_out, or_23_out, or_24_out, or_25_out, or_26_out,
       or_27_out, or_28_out, or_29_out, or_30_out, or_31_out, or_32_out,
       or_32bit_2input_implementation_1_out_3, or_32bit_5input_implementation_1_out_6, or_33_out, or_34_out,
       or_35_out, or_36_out, or_37_out, or_38_out, or_39_out, or_40_out, or_41_out, or_42_out, or_43_out,
       or_44_out, or_45_out, or_46_out, or_47_out, or_48_out, or_49_out, or_50_out, or_51_out, or_52_out,
       or_53_out, or_54_out, or_55_out, or_56_out, or_57_out, or_58_out, or_59_out, or_60_out, or_61_out,
       or_62_out, PC_q, register_6_q, register_7_q, register_8_q, register_9_q, register_10_q, register_11_q,
       register_12_q, register_13_q, register_14_q, register_15_q, register_16_q, register_17_q,
       register_18_q, register_19_q, register_20_q, register_21_q, register_22_q, register_23_q,
       register_24_q, register_25_q, register_26_q, register_27_q, register_28_q, register_29_q,
       register_30_q, register_31_q, register_32_q, register_33_q, register_34_q, register_35_q,
       register_36_q, register_37_q, register_38_q, register_39_q, shifter_1_out, shifter_2_out,
       shifter_3_out, subtractor_1_out, xor_32bit_2input_implementation_1_out_3;

  Clock clock_1 (.out(clock_1_out));
  RAM #(.addrWidth(24), .dataWidth(32), .trigger("high"), .databus("bibus")) IMEM (
    .addr(PC_q[25:2]), .we(1'b0), .oe(1'b1), .dout(IMEM_dout));  // open: din
  RAM #(.addrWidth(24), .dataWidth(32), .trigger("falling"), .databus("bibus")) DMEM (
    .addr(and_2_out), .we(and_1_out), .oe(1'b1), .clk(clock_1_out), .din(or_2_out), .dout(DMEM_dout));
  Comparator #(.width(6), .mode("unsigned")) comparator_1 (
    .a(multiplexer_10_out[31:26]), .b({6{1'b0}}), .eq(comparator_1_eq));  // open: gt, lt
  and and_1 (and_1_out, decoder_2_out8, comparator_1_eq);
  assign bit_extender_1_out = {{23{comparator_1_eq}}, comparator_1_eq};  // Bit_Extender bit_extender_1
  assign and_2_out = bit_extender_1_out & multiplexer_10_out[25:2];  // AND_Gate and_2, 24 bits wide
  Comparator #(.width(6), .mode("unsigned")) comparator_2 (
    .a(multiplexer_10_out[31:26]), .b({6{1'b0}}), .gt(comparator_2_gt));  // open: eq, lt
  Comparator #(.width(32)) comparator_3 (
    .a(or_1_out), .b(or_2_out), .eq(comparator_3_eq), .lt(comparator_3_lt));  // open: gt
  Comparator #(.width(32), .mode("unsigned")) comparator_4 (
    .a(or_1_out), .b(or_2_out), .eq(comparator_4_eq), .lt(comparator_4_lt));  // open: gt
  assign bit_extender_2_out = {{23{comparator_2_gt}}, comparator_2_gt};  // Bit_Extender bit_extender_2
  TTY tty_1 (.data(DMEM_dout[6:0]), .clk(clock_1_out));  // open: we, clr
  Adder #(.width(32)) adder_1 (.a(PC_q), .b(32'h4), .out(adder_1_out));  // open: cin, cout
  Register #(.width(32)) PC (.D(multiplexer_1_out), .en(1'b1), .clk(clock_1_out), .Q(PC_q));  // open: clr
  Multiplexer #(.width(32), .enable("false")) multiplexer_1 (
    .in0(adder_1_out), .in1(multiplexer_10_out), .out(multiplexer_1_out),
    .sel(or_1bit_3input_implementation_2_p3));
  Multiplexer #(.enable("false")) multiplexer_2 (
    .in0(comparator_3_eq), .in1(comparator_4_eq), .out(multiplexer_2_out), .sel(IMEM_dout[13]));
  Multiplexer #(.enable("false")) multiplexer_3 (
    .in0(comparator_3_lt), .in1(comparator_4_lt), .out(multiplexer_3_out), .sel(IMEM_dout[13]));
  AND_24bit_implementation and_24bit_implementation_1 (
    .in_2(bit_extender_2_out), .in_1(multiplexer_10_out[25:2]));  // open: out_3
  Decoder #(.select(3)) decoder_1 (
    .out0(decoder_1_out0), .out1(decoder_1_out1), .out2(decoder_1_out2), .out3(decoder_1_out3),
    .out4(decoder_1_out4), .out5(decoder_1_out5), .out6(decoder_1_out6), .out7(decoder_1_out7),
    .sel(undriven), .en(and_1bit_implementation_1_out_3));
  AND_1bit_Implementation and_1bit_implementation_1 (
    .out_3(and_1bit_implementation_1_out_3), .in_1(comparator_2_gt), .in_2(decoder_2_out8));
  OR_1bit_3Input_Implementation or_1bit_3input_implementation_1 (
    .in_3(decoder_2_out0[0]), .out_4(or_1bit_3input_implementation_1_out_4), .in_2(decoder_2_out4),
    .in_1(decoder_2_out25));
  assign bit_extender_3_out = {{31{or_1bit_3input_implementation_1_out_4}}, or_1bit_3input_implementation_1_out_4};  // Bit_Extender bit_extender_3
  assign bit_extender_4_out = {{20{IMEM_dout[31]}}, IMEM_dout[31:20]};  // Bit_Extender bit_extender_4
  assign bit_extender_5_out = {{31{decoder_2_out8}}, decoder_2_out8};  // Bit_Extender bit_extender_5
  AND_32bit_Implementation and_32bit_implementation_1 (
    .in_2(bit_extender_6_out), .out_3(and_32bit_implementation_1_out_3), .in_1(bit_extender_5_out));
  assign bit_extender_6_out = {{20{IMEM_dout[31]}}, {IMEM_dout[31:25], IMEM_dout[11:7]}};  // Bit_Extender bit_extender_6
  assign bit_extender_7_out = {{31{decoder_2_out24}}, decoder_2_out24};  // Bit_Extender bit_extender_7
  AND_32bit_Implementation and_32bit_implementation_2 (
    .in_2(bit_extender_8_out), .out_3(and_32bit_implementation_2_out_3), .in_1(bit_extender_7_out));
  assign bit_extender_8_out = {{19{IMEM_dout[31]}}, {IMEM_dout[31], IMEM_dout[7], IMEM_dout[30:25], IMEM_dout[11:8], 1'b0}};  // Bit_Extender bit_extender_8
  assign bit_extender_9_out = {{31{or_2input_implementation_2_out_3}}, or_2input_implementation_2_out_3};  // Bit_Extender bit_extender_9
  AND_32bit_Implementation and_32bit_implementation_3 (
    .in_2({IMEM_dout[31:12], {12{1'b0}}}), .out_3(and_32bit_implementation_3_out_3), .in_1(bit_extender_9_out));
  assign bit_extender_10_out = {{31{decoder_2_out27}}, decoder_2_out27};  // Bit_Extender bit_extender_10
  AND_32bit_Implementation and_32bit_implementation_4 (
    .in_2(bit_extender_11_out), .out_3(and_32bit_implementation_4_out_3), .in_1(bit_extender_10_out));
  assign bit_extender_11_out = {{11{IMEM_dout[31]}}, {IMEM_dout[31], IMEM_dout[19:12], IMEM_dout[20], IMEM_dout[30:21], 1'b0}};  // Bit_Extender bit_extender_11
  XOR_1bit_2Input_Implementation xor_1bit_2input_implementation_1 (
    .in_2(multiplexer_2_out), .out_3(xor_1bit_2input_implementation_1_out_3), .in_1(IMEM_dout[12]));
  XOR_1bit_2Input_Implementation xor_1bit_2input_implementation_2 (
    .in_2(multiplexer_3_out), .out_3(xor_1bit_2input_implementation_2_out_3), .in_1(IMEM_dout[12]));
  Register #(.width(32)) register_1 (
    .D(or_2_out), .en(decoder_1_out0), .clk(clock_1_out), .Q({register_1_q_2, register_1_q}));  // open: clr
  Register #(.width(32)) register_2 (
    .D(or_2_out), .en(decoder_1_out4), .clk(clock_1_out), .Q({register_2_q_2, register_2_q}));  // open: clr
  Decoder #(.select(5), .enable("false")) decoder_2 (
    .out0(decoder_2_out0[0]), .out4(decoder_2_out4), .out5(decoder_2_out5), .out8(decoder_2_out8),
    .out12(decoder_2_out12), .out13(decoder_2_out13), .out24(decoder_2_out24), .out25(decoder_2_out25),
    .out27(decoder_2_out27), .sel(IMEM_dout[6:2]));  // open: out1, out2, out3, out6, out7, out9, out10, out11, out14, out15, out16, out17, out18, out19, out20, out21, out22, out23, out26, out28, out29, out30, out31
  AND_32bit_Implementation and_32bit_implementation_5 (
    .in_2(bit_extender_4_out), .out_3(and_32bit_implementation_5_out_3), .in_1(bit_extender_3_out));
  OR_32bit_5Input_implementation or_32bit_5input_implementation_1 (
    .in_5(and_32bit_implementation_4_out_3), .in_2(and_32bit_implementation_1_out_3),
    .in_4(and_32bit_implementation_3_out_3), .out_6(or_32bit_5input_implementation_1_out_6),
    .in_1(and_32bit_implementation_5_out_3), .in_3(and_32bit_implementation_2_out_3));
  and and_3 (and_3_out, ~IMEM_dout[14], xor_1bit_2input_implementation_1_out_3);  // AND_Gate
  OR_2Input_Implementation or_2input_implementation_1 (
    .out_3(or_2input_implementation_1_out_3), .in_1(and_3_out), .in_2(and_1bit_implementation_2_out_3));
  AND_1bit_Implementation and_1bit_implementation_2 (
    .out_3(and_1bit_implementation_2_out_3), .in_1(IMEM_dout[14]),
    .in_2(xor_1bit_2input_implementation_2_out_3));
  OR_2Input_Implementation or_2input_implementation_2 (
    .out_3(or_2input_implementation_2_out_3), .in_1(decoder_2_out13), .in_2(decoder_2_out5));
  Register #(.width(32)) register_3 (
    .D(or_2_out), .en(decoder_1_out1), .clk(clock_1_out), .Q({register_3_q_2, register_3_q}));  // open: clr
  Register #(.width(32)) register_4 (
    .D(or_2_out), .en(decoder_1_out5), .clk(clock_1_out), .Q({register_4_q_2, register_4_q}));  // open: clr
  AND_1bit_Implementation and_1bit_implementation_3 (
    .out_3(and_1bit_implementation_3_out_3), .in_1(decoder_2_out24), .in_2(or_2input_implementation_1_out_3));
  Multiplexer #(.width(32), .enable("false")) multiplexer_4 (
    .in0(or_1_out), .in1(PC_q), .out(multiplexer_4_out), .sel(and_1bit_implementation_4_out_3));
  Multiplexer #(.width(32), .enable("false")) multiplexer_5 (
    .in0(or_2_out), .in1(or_32bit_5input_implementation_1_out_6), .out(multiplexer_5_out), .sel(not_1_out));
  Adder #(.width(32)) adder_2 (.a(multiplexer_4_out), .b(multiplexer_5_out), .out(adder_2_out));  // open: cin, cout
  Subtractor #(.width(32)) subtractor_1 (
    .a(multiplexer_4_out), .b(multiplexer_5_out), .out(subtractor_1_out));  // open: bin, bout
  Shifter #(.width(32)) shifter_1 (.in(multiplexer_4_out), .\dist (multiplexer_5_out[4:0]), .out(shifter_1_out));
  Comparator #(.width(32)) comparator_5 (
    .a(multiplexer_4_out), .b(multiplexer_5_out), .lt(comparator_5_lt));  // open: gt, eq
  Comparator #(.width(32), .mode("unsigned")) comparator_6 (
    .a(multiplexer_4_out), .b(multiplexer_5_out), .lt(comparator_6_lt));  // open: gt, eq
  XOR_32bit_2Input_Implementation xor_32bit_2input_implementation_1 (
    .out_3(xor_32bit_2input_implementation_1_out_3), .in_1(multiplexer_4_out), .in_2(multiplexer_5_out));
  Shifter #(.width(32), .shift("lr")) shifter_2 (
    .in(multiplexer_4_out), .\dist (multiplexer_5_out[4:0]), .out(shifter_2_out));
  Shifter #(.width(32), .shift("ar")) shifter_3 (
    .in(multiplexer_4_out), .\dist (multiplexer_5_out[4:0]), .out(shifter_3_out));
  OR_32bit_2Input_Implementation or_32bit_2input_implementation_1 (
    .in_2(multiplexer_5_out), .out_3(or_32bit_2input_implementation_1_out_3), .in_1(multiplexer_4_out));
  AND_32bit_Implementation and_32bit_implementation_6 (
    .in_2(multiplexer_5_out), .out_3(and_32bit_implementation_6_out_3), .in_1(multiplexer_4_out));
  Register #(.width(32)) register_5 (
    .D(or_2_out), .en(decoder_1_out2), .clk(clock_1_out), .Q({register_5_q_2, register_5_q}));  // open: clr
  Register #(.width(32)) register_6 (
    .D(or_2_out), .en(decoder_1_out6), .clk(clock_1_out), .Q(register_6_q));  // open: clr
  not not_1 (not_1_out, decoder_2_out12);
  AND_1bit_Implementation and_1bit_implementation_4 (
    .out_3(and_1bit_implementation_4_out_3), .in_1(decoder_2_out24), .in_2(decoder_2_out27));
  // OR_1bit_3Input_Implementation or_1bit_3input_implementation_2: pin names not known; wires that end beside it: and_1bit_implementation_3_out_3, decoder_2_out25, or_1bit_3input_implementation_2_p3, decoder_2_out27
  Multiplexer #(.width(32), .enable("false")) multiplexer_6 (
    .in0(adder_2_out), .in1(subtractor_1_out), .out(multiplexer_6_out), .sel(IMEM_dout[30]));
  assign bit_extender_12_out = {{31{1'b0}}, comparator_5_lt};  // Bit_Extender bit_extender_12
  assign bit_extender_13_out = {{31{1'b0}}, comparator_6_lt};  // Bit_Extender bit_extender_13
  Multiplexer #(.width(32), .enable("false")) multiplexer_7 (
    .in0(shifter_2_out), .in1(shifter_3_out), .out(multiplexer_7_out), .sel(IMEM_dout[30]));
  AND_1bit_Implementation and_1bit_implementation_5 (
    .out_3(and_1bit_implementation_5_out_3), .in_1(decoder_2_out12), .in_2(decoder_2_out4));
  AND_1bit_Implementation and_1bit_implementation_6 (
    .out_3(decoder_2_out0[1]), .in_1(decoder_2_out27), .in_2(decoder_2_out25));
  Multiplexer #(.select(3), .width(32), .enable("false")) multiplexer_8 (
    .in0(multiplexer_6_out), .in1(shifter_1_out), .in2(bit_extender_12_out), .in3(bit_extender_13_out),
    .in4(xor_32bit_2input_implementation_1_out_3), .in5(multiplexer_7_out),
    .in6(or_32bit_2input_implementation_1_out_3), .in7(and_32bit_implementation_6_out_3),
    .out(multiplexer_8_out), .sel(IMEM_dout[14:12]));
  Register #(.width(32)) register_7 (
    .D(or_2_out), .en(decoder_1_out3), .clk(clock_1_out), .Q(register_7_q));  // open: clr
  Register #(.width(32)) register_8 (
    .D(or_2_out), .en(decoder_1_out7), .clk(clock_1_out), .Q(register_8_q));  // open: clr
  nor nor_1 (nor_1_out, decoder_2_out8, decoder_2_out24);
  Multiplexer #(.width(32), .enable("false")) multiplexer_9 (
    .in0(adder_2_out), .in1(multiplexer_8_out), .out(multiplexer_9_out), .sel(and_1bit_implementation_5_out_3));
  Multiplexer #(.width(32), .enable("false")) multiplexer_10 (
    .in0(multiplexer_9_out), .in1(multiplexer_5_out), .out(multiplexer_10_out), .sel(decoder_2_out13));
  Multiplexer #(.select(2), .width(32), .enable("false")) multiplexer_11 (
    .in0(multiplexer_10_out), .in1(DMEM_dout), .in2(adder_1_out), .out(multiplexer_11_out),
    .sel(decoder_2_out0));  // open: in3
  and and_4 (and_4_out, ~IMEM_dout[15], ~IMEM_dout[16], ~IMEM_dout[17], ~IMEM_dout[18], ~IMEM_dout[19]);  // AND_Gate
  and and_5 (and_5_out, ~IMEM_dout[20], ~IMEM_dout[21], ~IMEM_dout[22], ~IMEM_dout[23], ~IMEM_dout[24]);  // AND_Gate
  and and_6 (and_6_out, nor_1_out, and_7_out);
  and and_7 (and_7_out, IMEM_dout[7], ~IMEM_dout[8], ~IMEM_dout[9], ~IMEM_dout[10], ~IMEM_dout[11]);  // AND_Gate
  and and_8 (and_8_out, IMEM_dout[15], ~IMEM_dout[16], ~IMEM_dout[17], ~IMEM_dout[18], ~IMEM_dout[19]);  // AND_Gate
  and and_9 (and_9_out, IMEM_dout[20], ~IMEM_dout[21], ~IMEM_dout[22], ~IMEM_dout[23], ~IMEM_dout[24]);  // AND_Gate
  and and_10 (and_10_out, nor_1_out, and_11_out);
  and and_11 (and_11_out, ~IMEM_dout[7], IMEM_dout[8], ~IMEM_dout[9], ~IMEM_dout[10], ~IMEM_dout[11]);  // AND_Gate
  and and_12 (and_12_out, ~IMEM_dout[15], IMEM_dout[16], ~IMEM_dout[17], ~IMEM_dout[18], ~IMEM_dout[19]);  // AND_Gate
  and and_13 (and_13_out, ~IMEM_dout[20], IMEM_dout[21], ~IMEM_dout[22], ~IMEM_dout[23], ~IMEM_dout[24]);  // AND_Gate
  and and_14 (and_14_out, nor_1_out, and_15_out);
  and and_15 (and_15_out, IMEM_dout[7], IMEM_dout[8], ~IMEM_dout[9], ~IMEM_dout[10], ~IMEM_dout[11]);  // AND_Gate
  and and_16 (and_16_out, IMEM_dout[15], IMEM_dout[16], ~IMEM_dout[17], ~IMEM_dout[18], ~IMEM_dout[19]);  // AND_Gate
  and and_17 (and_17_out, IMEM_dout[20], IMEM_dout[21], ~IMEM_dout[22], ~IMEM_dout[23], ~IMEM_dout[24]);  // AND_Gate
  and and_18 (and_18_out, nor_1_out, and_19_out);
  and and_19 (and_19_out, ~IMEM_dout[7], ~IMEM_dout[8], IMEM_dout[9], ~IMEM_dout[10], ~IMEM_dout[11]);  // AND_Gate
  and and_20 (and_20_out, ~IMEM_dout[15], ~IMEM_dout[16], IMEM_dout[17], ~IMEM_dout[18], ~IMEM_dout[19]);  // AND_Gate
  and and_21 (and_21_out, ~IMEM_dout[20], ~IMEM_dout[21], IMEM_dout[22], ~IMEM_dout[23], ~IMEM_dout[24]);  // AND_Gate
  and and_22 (and_22_out, nor_1_out, and_23_out);
  and and_23 (and_23_out, IMEM_dout[7], ~IMEM_dout[8], IMEM_dout[9], ~IMEM_dout[10], ~IMEM_dout[11]);  // AND_Gate
  and and_24 (and_24_out, IMEM_dout[15], ~IMEM_dout[16], IMEM_dout[17], ~IMEM_dout[18], ~IMEM_dout[19]);  // AND_Gate
  and and_25 (and_25_out, IMEM_dout[20], ~IMEM_dout[21], IMEM_dout[22], ~IMEM_dout[23], ~IMEM_dout[24]);  // AND_Gate
  and and_26 (and_26_out, nor_1_out, and_27_out);
  and and_27 (and_27_out, ~IMEM_dout[7], IMEM_dout[8], IMEM_dout[9], ~IMEM_dout[10], ~IMEM_dout[11]);  // AND_Gate
  and and_28 (and_28_out, ~IMEM_dout[15], IMEM_dout[16], IMEM_dout[17], ~IMEM_dout[18], ~IMEM_dout[19]);  // AND_Gate
  and and_29 (and_29_out, ~IMEM_dout[20], IMEM_dout[21], IMEM_dout[22], ~IMEM_dout[23], ~IMEM_dout[24]);  // AND_Gate
  and and_30 (and_30_out, nor_1_out, and_31_out);
  and and_31 (and_31_out, IMEM_dout[7], IMEM_dout[8], IMEM_dout[9], ~IMEM_dout[10], ~IMEM_dout[11]);  // AND_Gate
  and and_32 (and_32_out, IMEM_dout[15], IMEM_dout[16], IMEM_dout[17], ~IMEM_dout[18], ~IMEM_dout[19]);  // AND_Gate
  and and_33 (and_33_out, IMEM_dout[20], IMEM_dout[21], IMEM_dout[22], ~IMEM_dout[23], ~IMEM_dout[24]);  // AND_Gate
  Register #(.width(32)) register_9 (
    .D(multiplexer_11_out), .en(and_6_out), .clk(clock_1_out), .Q(register_9_q));  // open: clr
  Register #(.width(32)) register_10 (
    .D(multiplexer_11_out), .en(and_10_out), .clk(clock_1_out), .Q(register_10_q));  // open: clr
  Register #(.width(32)) register_11 (
    .D(multiplexer_11_out), .en(and_14_out), .clk(clock_1_out), .Q(register_11_q));  // open: clr
  Register #(.width(32)) register_12 (
    .D(multiplexer_11_out), .en(and_18_out), .clk(clock_1_out), .Q(register_12_q));  // open: clr
  Register #(.width(32)) register_13 (
    .D(multiplexer_11_out), .en(and_22_out), .clk(clock_1_out), .Q(register_13_q));  // open: clr
  Register #(.width(32)) register_14 (
    .D(multiplexer_11_out), .en(and_26_out), .clk(clock_1_out), .Q(register_14_q));  // open: clr
  Register #(.width(32)) register_15 (
    .D(multiplexer_11_out), .en(and_30_out), .clk(clock_1_out), .Q(register_15_q));  // open: clr
  assign or_1_out = or_17_out | or_3_out;  // OR_Gate or_1, 32 bits wide
  assign or_2_out = or_18_out | or_4_out;  // OR_Gate or_2, 32 bits wide
  assign and_34_out = {32{1'b0}} & bit_extender_14_out;  // AND_Gate and_34, 32 bits wide
  assign and_35_out = {32{1'b0}} & bit_extender_15_out;  // AND_Gate and_35, 32 bits wide
  assign bit_extender_14_out = {{31{and_4_out}}, and_4_out};  // Bit_Extender bit_extender_14
  assign bit_extender_15_out = {{31{and_5_out}}, and_5_out};  // Bit_Extender bit_extender_15
  assign and_36_out = register_9_q & bit_extender_16_out;  // AND_Gate and_36, 32 bits wide
  assign and_37_out = register_9_q & bit_extender_17_out;  // AND_Gate and_37, 32 bits wide
  assign bit_extender_16_out = {{31{and_8_out}}, and_8_out};  // Bit_Extender bit_extender_16
  assign bit_extender_17_out = {{31{and_9_out}}, and_9_out};  // Bit_Extender bit_extender_17
  assign and_38_out = register_10_q & bit_extender_18_out;  // AND_Gate and_38, 32 bits wide
  assign and_39_out = register_10_q & bit_extender_19_out;  // AND_Gate and_39, 32 bits wide
  assign bit_extender_18_out = {{31{and_12_out}}, and_12_out};  // Bit_Extender bit_extender_18
  assign bit_extender_19_out = {{31{and_13_out}}, and_13_out};  // Bit_Extender bit_extender_19
  assign and_40_out = register_11_q & bit_extender_20_out;  // AND_Gate and_40, 32 bits wide
  assign and_41_out = register_11_q & bit_extender_21_out;  // AND_Gate and_41, 32 bits wide
  assign bit_extender_20_out = {{31{and_16_out}}, and_16_out};  // Bit_Extender bit_extender_20
  assign bit_extender_21_out = {{31{and_17_out}}, and_17_out};  // Bit_Extender bit_extender_21
  assign and_42_out = register_12_q & bit_extender_22_out;  // AND_Gate and_42, 32 bits wide
  assign and_43_out = register_12_q & bit_extender_23_out;  // AND_Gate and_43, 32 bits wide
  assign bit_extender_22_out = {{31{and_20_out}}, and_20_out};  // Bit_Extender bit_extender_22
  assign bit_extender_23_out = {{31{and_21_out}}, and_21_out};  // Bit_Extender bit_extender_23
  assign and_44_out = register_13_q & bit_extender_24_out;  // AND_Gate and_44, 32 bits wide
  assign and_45_out = register_13_q & bit_extender_25_out;  // AND_Gate and_45, 32 bits wide
  assign bit_extender_24_out = {{31{and_24_out}}, and_24_out};  // Bit_Extender bit_extender_24
  assign bit_extender_25_out = {{31{and_25_out}}, and_25_out};  // Bit_Extender bit_extender_25
  assign and_46_out = register_14_q & bit_extender_26_out;  // AND_Gate and_46, 32 bits wide
  assign and_47_out = register_14_q & bit_extender_27_out;  // AND_Gate and_47, 32 bits wide
  assign bit_extender_26_out = {{31{and_28_out}}, and_28_out};  // Bit_Extender bit_extender_26
  assign bit_extender_27_out = {{31{and_29_out}}, and_29_out};  // Bit_Extender bit_extender_27
  assign and_48_out = register_15_q & bit_extender_28_out;  // AND_Gate and_48, 32 bits wide
  assign and_49_out = register_15_q & bit_extender_29_out;  // AND_Gate and_49, 32 bits wide
  assign bit_extender_28_out = {{31{and_32_out}}, and_32_out};  // Bit_Extender bit_extender_28
  assign bit_extender_29_out = {{31{and_33_out}}, and_33_out};  // Bit_Extender bit_extender_29
  assign or_3_out = and_34_out | or_5_out;  // OR_Gate or_3, 32 bits wide
  assign or_4_out = and_35_out | or_6_out;  // OR_Gate or_4, 32 bits wide
  assign or_5_out = and_36_out | or_7_out;  // OR_Gate or_5, 32 bits wide
  assign or_6_out = and_37_out | or_8_out;  // OR_Gate or_6, 32 bits wide
  assign or_7_out = and_38_out | or_9_out;  // OR_Gate or_7, 32 bits wide
  assign or_8_out = and_39_out | or_10_out;  // OR_Gate or_8, 32 bits wide
  assign or_9_out = and_40_out | or_11_out;  // OR_Gate or_9, 32 bits wide
  assign or_10_out = and_41_out | or_12_out;  // OR_Gate or_10, 32 bits wide
  assign or_11_out = and_42_out | or_13_out;  // OR_Gate or_11, 32 bits wide
  assign or_12_out = and_43_out | or_14_out;  // OR_Gate or_12, 32 bits wide
  assign or_13_out = and_44_out | or_15_out;  // OR_Gate or_13, 32 bits wide
  assign or_14_out = and_45_out | or_16_out;  // OR_Gate or_14, 32 bits wide
  assign or_15_out = and_46_out | and_48_out;  // OR_Gate or_15, 32 bits wide
  assign or_16_out = and_47_out | and_49_out;  // OR_Gate or_16, 32 bits wide
  and and_50 (and_50_out, ~IMEM_dout[7], ~IMEM_dout[8], ~IMEM_dout[9], IMEM_dout[10], ~IMEM_dout[11]);  // AND_Gate
  and and_51 (and_51_out, ~IMEM_dout[15], ~IMEM_dout[16], ~IMEM_dout[17], IMEM_dout[18], ~IMEM_dout[19]);  // AND_Gate
  and and_52 (and_52_out, ~IMEM_dout[20], ~IMEM_dout[21], ~IMEM_dout[22], IMEM_dout[23], ~IMEM_dout[24]);  // AND_Gate
  and and_53 (and_53_out, IMEM_dout[7], ~IMEM_dout[8], ~IMEM_dout[9], IMEM_dout[10], ~IMEM_dout[11]);  // AND_Gate
  and and_54 (and_54_out, IMEM_dout[15], ~IMEM_dout[16], ~IMEM_dout[17], IMEM_dout[18], ~IMEM_dout[19]);  // AND_Gate
  and and_55 (and_55_out, IMEM_dout[20], ~IMEM_dout[21], ~IMEM_dout[22], IMEM_dout[23], ~IMEM_dout[24]);  // AND_Gate
  and and_56 (and_56_out, ~IMEM_dout[7], IMEM_dout[8], ~IMEM_dout[9], IMEM_dout[10], ~IMEM_dout[11]);  // AND_Gate
  and and_57 (and_57_out, ~IMEM_dout[15], IMEM_dout[16], ~IMEM_dout[17], IMEM_dout[18], ~IMEM_dout[19]);  // AND_Gate
  and and_58 (and_58_out, ~IMEM_dout[20], IMEM_dout[21], ~IMEM_dout[22], IMEM_dout[23], ~IMEM_dout[24]);  // AND_Gate
  and and_59 (and_59_out, IMEM_dout[7], IMEM_dout[8], ~IMEM_dout[9], IMEM_dout[10], ~IMEM_dout[11]);  // AND_Gate
  and and_60 (and_60_out, IMEM_dout[15], IMEM_dout[16], ~IMEM_dout[17], IMEM_dout[18], ~IMEM_dout[19]);  // AND_Gate
  and and_61 (and_61_out, IMEM_dout[20], IMEM_dout[21], ~IMEM_dout[22], IMEM_dout[23], ~IMEM_dout[24]);  // AND_Gate
  and and_62 (and_62_out, ~IMEM_dout[7], ~IMEM_dout[8], IMEM_dout[9], IMEM_dout[10], ~IMEM_dout[11]);  // AND_Gate
  and and_63 (and_63_out, ~IMEM_dout[15], ~IMEM_dout[16], IMEM_dout[17], IMEM_dout[18], ~IMEM_dout[19]);  // AND_Gate
  and and_64 (and_64_out, ~IMEM_dout[20], ~IMEM_dout[21], IMEM_dout[22], IMEM_dout[23], ~IMEM_dout[24]);  // AND_Gate
  and and_65 (and_65_out, IMEM_dout[7], ~IMEM_dout[8], IMEM_dout[9], IMEM_dout[10], ~IMEM_dout[11]);  // AND_Gate
  and and_66 (and_66_out, IMEM_dout[15], ~IMEM_dout[16], IMEM_dout[17], IMEM_dout[18], ~IMEM_dout[19]);  // AND_Gate
  and and_67 (and_67_out, IMEM_dout[20], ~IMEM_dout[21], IMEM_dout[22], IMEM_dout[23], ~IMEM_dout[24]);  // AND_Gate
  and and_68 (and_68_out, ~IMEM_dout[7], IMEM_dout[8], IMEM_dout[9], IMEM_dout[10], ~IMEM_dout[11]);  // AND_Gate
  and and_69 (and_69_out, ~IMEM_dout[15], IMEM_dout[16], IMEM_dout[17], IMEM_dout[18], ~IMEM_dout[19]);  // AND_Gate
  and and_70 (and_70_out, ~IMEM_dout[20], IMEM_dout[21], IMEM_dout[22], IMEM_dout[23], ~IMEM_dout[24]);  // AND_Gate
  and and_71 (and_71_out, IMEM_dout[7], IMEM_dout[8], IMEM_dout[9], IMEM_dout[10], ~IMEM_dout[11]);  // AND_Gate
  and and_72 (and_72_out, IMEM_dout[15], IMEM_dout[16], IMEM_dout[17], IMEM_dout[18], ~IMEM_dout[19]);  // AND_Gate
  and and_73 (and_73_out, IMEM_dout[20], IMEM_dout[21], IMEM_dout[22], IMEM_dout[23], ~IMEM_dout[24]);  // AND_Gate
  Register #(.width(32)) register_16 (
    .D(multiplexer_11_out), .en(and_74_out), .clk(clock_1_out), .Q(register_16_q));  // open: clr
  and and_74 (and_74_out, nor_1_out, and_50_out);
  Register #(.width(32)) register_17 (
    .D(multiplexer_11_out), .en(and_75_out), .clk(clock_1_out), .Q(register_17_q));  // open: clr
  and and_75 (and_75_out, nor_1_out, and_53_out);
  Register #(.width(32)) register_18 (
    .D(multiplexer_11_out), .en(and_76_out), .clk(clock_1_out), .Q(register_18_q));  // open: clr
  and and_76 (and_76_out, nor_1_out, and_56_out);
  Register #(.width(32)) register_19 (
    .D(multiplexer_11_out), .en(and_77_out), .clk(clock_1_out), .Q(register_19_q));  // open: clr
  and and_77 (and_77_out, nor_1_out, and_59_out);
  Register #(.width(32)) register_20 (
    .D(multiplexer_11_out), .en(and_78_out), .clk(clock_1_out), .Q(register_20_q));  // open: clr
  and and_78 (and_78_out, nor_1_out, and_62_out);
  Register #(.width(32)) register_21 (
    .D(multiplexer_11_out), .en(and_79_out), .clk(clock_1_out), .Q(register_21_q));  // open: clr
  and and_79 (and_79_out, nor_1_out, and_65_out);
  Register #(.width(32)) register_22 (
    .D(multiplexer_11_out), .en(and_80_out), .clk(clock_1_out), .Q(register_22_q));  // open: clr
  and and_80 (and_80_out, nor_1_out, and_68_out);
  Register #(.width(32)) register_23 (
    .D(multiplexer_11_out), .en(and_81_out), .clk(clock_1_out), .Q(register_23_q));  // open: clr
  and and_81 (and_81_out, nor_1_out, and_71_out);
  assign or_17_out = or_33_out | or_19_out;  // OR_Gate or_17, 32 bits wide
  assign bit_extender_30_out = {{31{and_51_out}}, and_51_out};  // Bit_Extender bit_extender_30
  assign bit_extender_31_out = {{31{and_52_out}}, and_52_out};  // Bit_Extender bit_extender_31
  assign bit_extender_32_out = {{31{and_54_out}}, and_54_out};  // Bit_Extender bit_extender_32
  assign bit_extender_33_out = {{31{and_55_out}}, and_55_out};  // Bit_Extender bit_extender_33
  assign bit_extender_34_out = {{31{and_57_out}}, and_57_out};  // Bit_Extender bit_extender_34
  assign bit_extender_35_out = {{31{and_58_out}}, and_58_out};  // Bit_Extender bit_extender_35
  assign bit_extender_36_out = {{31{and_60_out}}, and_60_out};  // Bit_Extender bit_extender_36
  assign bit_extender_37_out = {{31{and_61_out}}, and_61_out};  // Bit_Extender bit_extender_37
  assign bit_extender_38_out = {{31{and_63_out}}, and_63_out};  // Bit_Extender bit_extender_38
  assign bit_extender_39_out = {{31{and_64_out}}, and_64_out};  // Bit_Extender bit_extender_39
  assign bit_extender_40_out = {{31{and_66_out}}, and_66_out};  // Bit_Extender bit_extender_40
  assign bit_extender_41_out = {{31{and_67_out}}, and_67_out};  // Bit_Extender bit_extender_41
  assign bit_extender_42_out = {{31{and_69_out}}, and_69_out};  // Bit_Extender bit_extender_42
  assign bit_extender_43_out = {{31{and_70_out}}, and_70_out};  // Bit_Extender bit_extender_43
  assign bit_extender_44_out = {{31{and_72_out}}, and_72_out};  // Bit_Extender bit_extender_44
  assign bit_extender_45_out = {{31{and_73_out}}, and_73_out};  // Bit_Extender bit_extender_45
  assign or_18_out = or_34_out | or_20_out;  // OR_Gate or_18, 32 bits wide
  assign or_19_out = and_82_out | or_21_out;  // OR_Gate or_19, 32 bits wide
  assign or_20_out = and_83_out | or_22_out;  // OR_Gate or_20, 32 bits wide
  assign and_82_out = register_16_q & bit_extender_30_out;  // AND_Gate and_82, 32 bits wide
  assign and_83_out = register_16_q & bit_extender_31_out;  // AND_Gate and_83, 32 bits wide
  assign or_21_out = and_84_out | or_23_out;  // OR_Gate or_21, 32 bits wide
  assign or_22_out = and_85_out | or_24_out;  // OR_Gate or_22, 32 bits wide
  assign and_84_out = register_17_q & bit_extender_32_out;  // AND_Gate and_84, 32 bits wide
  assign and_85_out = register_17_q & bit_extender_33_out;  // AND_Gate and_85, 32 bits wide
  assign or_23_out = and_86_out | or_25_out;  // OR_Gate or_23, 32 bits wide
  assign or_24_out = and_87_out | or_26_out;  // OR_Gate or_24, 32 bits wide
  assign and_86_out = register_18_q & bit_extender_34_out;  // AND_Gate and_86, 32 bits wide
  assign and_87_out = register_18_q & bit_extender_35_out;  // AND_Gate and_87, 32 bits wide
  assign or_25_out = and_88_out | or_27_out;  // OR_Gate or_25, 32 bits wide
  assign or_26_out = and_89_out | or_28_out;  // OR_Gate or_26, 32 bits wide
  assign and_88_out = register_19_q & bit_extender_36_out;  // AND_Gate and_88, 32 bits wide
  assign and_89_out = register_19_q & bit_extender_37_out;  // AND_Gate and_89, 32 bits wide
  assign or_27_out = and_90_out | or_29_out;  // OR_Gate or_27, 32 bits wide
  assign or_28_out = and_91_out | or_30_out;  // OR_Gate or_28, 32 bits wide
  assign and_90_out = register_20_q & bit_extender_38_out;  // AND_Gate and_90, 32 bits wide
  assign and_91_out = register_20_q & bit_extender_39_out;  // AND_Gate and_91, 32 bits wide
  assign or_29_out = and_92_out | or_31_out;  // OR_Gate or_29, 32 bits wide
  assign or_30_out = and_93_out | or_32_out;  // OR_Gate or_30, 32 bits wide
  assign and_92_out = register_21_q & bit_extender_40_out;  // AND_Gate and_92, 32 bits wide
  assign and_93_out = register_21_q & bit_extender_41_out;  // AND_Gate and_93, 32 bits wide
  assign or_31_out = and_94_out | and_96_out;  // OR_Gate or_31, 32 bits wide
  assign or_32_out = and_95_out | and_97_out;  // OR_Gate or_32, 32 bits wide
  assign and_94_out = register_22_q & bit_extender_42_out;  // AND_Gate and_94, 32 bits wide
  assign and_95_out = register_22_q & bit_extender_43_out;  // AND_Gate and_95, 32 bits wide
  assign and_96_out = register_23_q & bit_extender_44_out;  // AND_Gate and_96, 32 bits wide
  assign and_97_out = register_23_q & bit_extender_45_out;  // AND_Gate and_97, 32 bits wide
  and and_98 (and_98_out, nor_1_out, and_99_out);
  and and_99 (and_99_out, ~IMEM_dout[7], ~IMEM_dout[8], ~IMEM_dout[9], ~IMEM_dout[10], IMEM_dout[11]);  // AND_Gate
  and and_100 (and_100_out, ~IMEM_dout[15], ~IMEM_dout[16], ~IMEM_dout[17], ~IMEM_dout[18], IMEM_dout[19]);  // AND_Gate
  and and_101 (and_101_out, ~IMEM_dout[20], ~IMEM_dout[21], ~IMEM_dout[22], ~IMEM_dout[23], IMEM_dout[24]);  // AND_Gate
  and and_102 (and_102_out, nor_1_out, and_103_out);
  and and_103 (and_103_out, IMEM_dout[7], ~IMEM_dout[8], ~IMEM_dout[9], ~IMEM_dout[10], IMEM_dout[11]);  // AND_Gate
  and and_104 (and_104_out, IMEM_dout[15], ~IMEM_dout[16], ~IMEM_dout[17], ~IMEM_dout[18], IMEM_dout[19]);  // AND_Gate
  and and_105 (and_105_out, IMEM_dout[20], ~IMEM_dout[21], ~IMEM_dout[22], ~IMEM_dout[23], IMEM_dout[24]);  // AND_Gate
  and and_106 (and_106_out, nor_1_out, and_107_out);
  and and_107 (and_107_out, ~IMEM_dout[7], IMEM_dout[8], ~IMEM_dout[9], ~IMEM_dout[10], IMEM_dout[11]);  // AND_Gate
  and and_108 (and_108_out, ~IMEM_dout[15], IMEM_dout[16], ~IMEM_dout[17], ~IMEM_dout[18], IMEM_dout[19]);  // AND_Gate
  and and_109 (and_109_out, ~IMEM_dout[20], IMEM_dout[21], ~IMEM_dout[22], ~IMEM_dout[23], IMEM_dout[24]);  // AND_Gate
  and and_110 (and_110_out, nor_1_out, and_111_out);
  and and_111 (and_111_out, IMEM_dout[7], IMEM_dout[8], ~IMEM_dout[9], ~IMEM_dout[10], IMEM_dout[11]);  // AND_Gate
  and and_112 (and_112_out, IMEM_dout[15], IMEM_dout[16], ~IMEM_dout[17], ~IMEM_dout[18], IMEM_dout[19]);  // AND_Gate
  and and_113 (and_113_out, IMEM_dout[20], IMEM_dout[21], ~IMEM_dout[22], ~IMEM_dout[23], IMEM_dout[24]);  // AND_Gate
  and and_114 (and_114_out, nor_1_out, and_115_out);
  and and_115 (and_115_out, ~IMEM_dout[7], ~IMEM_dout[8], IMEM_dout[9], ~IMEM_dout[10], IMEM_dout[11]);  // AND_Gate
  and and_116 (and_116_out, ~IMEM_dout[15], ~IMEM_dout[16], IMEM_dout[17], ~IMEM_dout[18], IMEM_dout[19]);  // AND_Gate
  and and_117 (and_117_out, ~IMEM_dout[20], ~IMEM_dout[21], IMEM_dout[22], ~IMEM_dout[23], IMEM_dout[24]);  // AND_Gate
  and and_118 (and_118_out, nor_1_out, and_119_out);
  and and_119 (and_119_out, IMEM_dout[7], ~IMEM_dout[8], IMEM_dout[9], ~IMEM_dout[10], IMEM_dout[11]);  // AND_Gate
  and and_120 (and_120_out, IMEM_dout[15], ~IMEM_dout[16], IMEM_dout[17], ~IMEM_dout[18], IMEM_dout[19]);  // AND_Gate
  and and_121 (and_121_out, IMEM_dout[20], ~IMEM_dout[21], IMEM_dout[22], ~IMEM_dout[23], IMEM_dout[24]);  // AND_Gate
  and and_122 (and_122_out, nor_1_out, and_123_out);
  and and_123 (and_123_out, ~IMEM_dout[7], IMEM_dout[8], IMEM_dout[9], ~IMEM_dout[10], IMEM_dout[11]);  // AND_Gate
  and and_124 (and_124_out, ~IMEM_dout[15], IMEM_dout[16], IMEM_dout[17], ~IMEM_dout[18], IMEM_dout[19]);  // AND_Gate
  and and_125 (and_125_out, ~IMEM_dout[20], IMEM_dout[21], IMEM_dout[22], ~IMEM_dout[23], IMEM_dout[24]);  // AND_Gate
  and and_126 (and_126_out, nor_1_out, and_127_out);
  and and_127 (and_127_out, IMEM_dout[7], IMEM_dout[8], IMEM_dout[9], ~IMEM_dout[10], IMEM_dout[11]);  // AND_Gate
  and and_128 (and_128_out, IMEM_dout[15], IMEM_dout[16], IMEM_dout[17], ~IMEM_dout[18], IMEM_dout[19]);  // AND_Gate
  and and_129 (and_129_out, IMEM_dout[20], IMEM_dout[21], IMEM_dout[22], ~IMEM_dout[23], IMEM_dout[24]);  // AND_Gate
  assign or_33_out = or_49_out | or_35_out;  // OR_Gate or_33, 32 bits wide
  Register #(.width(32)) register_24 (
    .D(multiplexer_11_out), .en(and_98_out), .clk(clock_1_out), .Q(register_24_q));  // open: clr
  assign bit_extender_46_out = {{31{and_100_out}}, and_100_out};  // Bit_Extender bit_extender_46
  assign bit_extender_47_out = {{31{and_101_out}}, and_101_out};  // Bit_Extender bit_extender_47
  Register #(.width(32)) register_25 (
    .D(multiplexer_11_out), .en(and_102_out), .clk(clock_1_out), .Q(register_25_q));  // open: clr
  assign bit_extender_48_out = {{31{and_104_out}}, and_104_out};  // Bit_Extender bit_extender_48
  assign bit_extender_49_out = {{31{and_105_out}}, and_105_out};  // Bit_Extender bit_extender_49
  Register #(.width(32)) register_26 (
    .D(multiplexer_11_out), .en(and_106_out), .clk(clock_1_out), .Q(register_26_q));  // open: clr
  assign bit_extender_50_out = {{31{and_108_out}}, and_108_out};  // Bit_Extender bit_extender_50
  assign bit_extender_51_out = {{31{and_109_out}}, and_109_out};  // Bit_Extender bit_extender_51
  Register #(.width(32)) register_27 (
    .D(multiplexer_11_out), .en(and_110_out), .clk(clock_1_out), .Q(register_27_q));  // open: clr
  assign bit_extender_52_out = {{31{and_112_out}}, and_112_out};  // Bit_Extender bit_extender_52
  assign bit_extender_53_out = {{31{and_113_out}}, and_113_out};  // Bit_Extender bit_extender_53
  Register #(.width(32)) register_28 (
    .D(multiplexer_11_out), .en(and_114_out), .clk(clock_1_out), .Q(register_28_q));  // open: clr
  assign bit_extender_54_out = {{31{and_116_out}}, and_116_out};  // Bit_Extender bit_extender_54
  assign bit_extender_55_out = {{31{and_117_out}}, and_117_out};  // Bit_Extender bit_extender_55
  Register #(.width(32)) register_29 (
    .D(multiplexer_11_out), .en(and_118_out), .clk(clock_1_out), .Q(register_29_q));  // open: clr
  assign bit_extender_56_out = {{31{and_120_out}}, and_120_out};  // Bit_Extender bit_extender_56
  assign bit_extender_57_out = {{31{and_121_out}}, and_121_out};  // Bit_Extender bit_extender_57
  Register #(.width(32)) register_30 (
    .D(multiplexer_11_out), .en(and_122_out), .clk(clock_1_out), .Q(register_30_q));  // open: clr
  assign bit_extender_58_out = {{31{and_124_out}}, and_124_out};  // Bit_Extender bit_extender_58
  assign bit_extender_59_out = {{31{and_125_out}}, and_125_out};  // Bit_Extender bit_extender_59
  Register #(.width(32)) register_31 (
    .D(multiplexer_11_out), .en(and_126_out), .clk(clock_1_out), .Q(register_31_q));  // open: clr
  assign bit_extender_60_out = {{31{and_128_out}}, and_128_out};  // Bit_Extender bit_extender_60
  assign bit_extender_61_out = {{31{and_129_out}}, and_129_out};  // Bit_Extender bit_extender_61
  assign or_34_out = or_50_out | or_42_out;  // OR_Gate or_34, 32 bits wide
  assign or_35_out = and_130_out | or_36_out;  // OR_Gate or_35, 32 bits wide
  assign and_130_out = register_24_q & bit_extender_46_out;  // AND_Gate and_130, 32 bits wide
  assign and_131_out = register_24_q & bit_extender_47_out;  // AND_Gate and_131, 32 bits wide
  assign or_36_out = and_132_out | or_37_out;  // OR_Gate or_36, 32 bits wide
  assign and_132_out = register_25_q & bit_extender_48_out;  // AND_Gate and_132, 32 bits wide
  assign and_133_out = register_25_q & bit_extender_49_out;  // AND_Gate and_133, 32 bits wide
  assign or_37_out = and_134_out | or_38_out;  // OR_Gate or_37, 32 bits wide
  assign and_134_out = register_26_q & bit_extender_50_out;  // AND_Gate and_134, 32 bits wide
  assign and_135_out = register_26_q & bit_extender_51_out;  // AND_Gate and_135, 32 bits wide
  assign or_38_out = and_136_out | or_39_out;  // OR_Gate or_38, 32 bits wide
  assign and_136_out = register_27_q & bit_extender_52_out;  // AND_Gate and_136, 32 bits wide
  assign and_137_out = register_27_q & bit_extender_53_out;  // AND_Gate and_137, 32 bits wide
  assign or_39_out = and_138_out | or_40_out;  // OR_Gate or_39, 32 bits wide
  assign and_138_out = register_28_q & bit_extender_54_out;  // AND_Gate and_138, 32 bits wide
  assign and_139_out = register_28_q & bit_extender_55_out;  // AND_Gate and_139, 32 bits wide
  assign or_40_out = and_140_out | or_41_out;  // OR_Gate or_40, 32 bits wide
  assign and_140_out = register_29_q & bit_extender_56_out;  // AND_Gate and_140, 32 bits wide
  assign and_141_out = register_29_q & bit_extender_57_out;  // AND_Gate and_141, 32 bits wide
  assign or_41_out = and_142_out | and_144_out;  // OR_Gate or_41, 32 bits wide
  assign and_142_out = register_30_q & bit_extender_58_out;  // AND_Gate and_142, 32 bits wide
  assign and_143_out = register_30_q & bit_extender_59_out;  // AND_Gate and_143, 32 bits wide
  assign and_144_out = register_31_q & bit_extender_60_out;  // AND_Gate and_144, 32 bits wide
  assign and_145_out = register_31_q & bit_extender_61_out;  // AND_Gate and_145, 32 bits wide
  assign or_42_out = and_131_out | or_43_out;  // OR_Gate or_42, 32 bits wide
  assign or_43_out = and_133_out | or_44_out;  // OR_Gate or_43, 32 bits wide
  assign or_44_out = and_135_out | or_45_out;  // OR_Gate or_44, 32 bits wide
  assign or_45_out = and_137_out | or_46_out;  // OR_Gate or_45, 32 bits wide
  assign or_46_out = and_139_out | or_47_out;  // OR_Gate or_46, 32 bits wide
  assign or_47_out = and_141_out | or_48_out;  // OR_Gate or_47, 32 bits wide
  assign or_48_out = and_143_out | and_145_out;  // OR_Gate or_48, 32 bits wide
  and and_146 (and_146_out, ~IMEM_dout[7], ~IMEM_dout[8], ~IMEM_dout[9], IMEM_dout[10], IMEM_dout[11]);  // AND_Gate
  and and_147 (and_147_out, ~IMEM_dout[15], ~IMEM_dout[16], ~IMEM_dout[17], IMEM_dout[18], IMEM_dout[19]);  // AND_Gate
  and and_148 (and_148_out, ~IMEM_dout[20], ~IMEM_dout[21], ~IMEM_dout[22], IMEM_dout[23], IMEM_dout[24]);  // AND_Gate
  and and_149 (and_149_out, IMEM_dout[7], ~IMEM_dout[8], ~IMEM_dout[9], IMEM_dout[10], IMEM_dout[11]);  // AND_Gate
  and and_150 (and_150_out, IMEM_dout[15], ~IMEM_dout[16], ~IMEM_dout[17], IMEM_dout[18], IMEM_dout[19]);  // AND_Gate
  and and_151 (and_151_out, IMEM_dout[20], ~IMEM_dout[21], ~IMEM_dout[22], IMEM_dout[23], IMEM_dout[24]);  // AND_Gate
  and and_152 (and_152_out, ~IMEM_dout[7], IMEM_dout[8], ~IMEM_dout[9], IMEM_dout[10], IMEM_dout[11]);  // AND_Gate
  and and_153 (and_153_out, ~IMEM_dout[15], IMEM_dout[16], ~IMEM_dout[17], IMEM_dout[18], IMEM_dout[19]);  // AND_Gate
  and and_154 (and_154_out, ~IMEM_dout[20], IMEM_dout[21], ~IMEM_dout[22], IMEM_dout[23], IMEM_dout[24]);  // AND_Gate
  and and_155 (and_155_out, IMEM_dout[7], IMEM_dout[8], ~IMEM_dout[9], IMEM_dout[10], IMEM_dout[11]);  // AND_Gate
  and and_156 (and_156_out, IMEM_dout[15], IMEM_dout[16], ~IMEM_dout[17], IMEM_dout[18], IMEM_dout[19]);  // AND_Gate
  and and_157 (and_157_out, IMEM_dout[20], IMEM_dout[21], ~IMEM_dout[22], IMEM_dout[23], IMEM_dout[24]);  // AND_Gate
  and and_158 (and_158_out, ~IMEM_dout[7], ~IMEM_dout[8], IMEM_dout[9], IMEM_dout[10], IMEM_dout[11]);  // AND_Gate
  and and_159 (and_159_out, ~IMEM_dout[15], ~IMEM_dout[16], IMEM_dout[17], IMEM_dout[18], IMEM_dout[19]);  // AND_Gate
  and and_160 (and_160_out, ~IMEM_dout[20], ~IMEM_dout[21], IMEM_dout[22], IMEM_dout[23], IMEM_dout[24]);  // AND_Gate
  and and_161 (and_161_out, IMEM_dout[7], ~IMEM_dout[8], IMEM_dout[9], IMEM_dout[10], IMEM_dout[11]);  // AND_Gate
  and and_162 (and_162_out, IMEM_dout[15], ~IMEM_dout[16], IMEM_dout[17], IMEM_dout[18], IMEM_dout[19]);  // AND_Gate
  and and_163 (and_163_out, IMEM_dout[20], ~IMEM_dout[21], IMEM_dout[22], IMEM_dout[23], IMEM_dout[24]);  // AND_Gate
  and and_164 (and_164_out, ~IMEM_dout[7], IMEM_dout[8], IMEM_dout[9], IMEM_dout[10], IMEM_dout[11]);  // AND_Gate
  and and_165 (and_165_out, ~IMEM_dout[15], IMEM_dout[16], IMEM_dout[17], IMEM_dout[18], IMEM_dout[19]);  // AND_Gate
  and and_166 (and_166_out, ~IMEM_dout[20], IMEM_dout[21], IMEM_dout[22], IMEM_dout[23], IMEM_dout[24]);  // AND_Gate
  and and_167 (and_167_out, IMEM_dout[7], IMEM_dout[8], IMEM_dout[9], IMEM_dout[10], IMEM_dout[11]);
  and and_168 (and_168_out, IMEM_dout[15], IMEM_dout[16], IMEM_dout[17], IMEM_dout[18], IMEM_dout[19]);
  and and_169 (and_169_out, IMEM_dout[20], IMEM_dout[21], IMEM_dout[22], IMEM_dout[23], IMEM_dout[24]);
  Register #(.width(32)) register_32 (
    .D(multiplexer_11_out), .en(and_170_out), .clk(clock_1_out), .Q(register_32_q));  // open: clr
  and and_170 (and_170_out, nor_1_out, and_146_out);
  Register #(.width(32)) register_33 (
    .D(multiplexer_11_out), .en(and_171_out), .clk(clock_1_out), .Q(register_33_q));  // open: clr
  and and_171 (and_171_out, nor_1_out, and_149_out);
  Register #(.width(32)) register_34 (
    .D(multiplexer_11_out), .en(and_172_out), .clk(clock_1_out), .Q(register_34_q));  // open: clr
  and and_172 (and_172_out, nor_1_out, and_152_out);
  Register #(.width(32)) register_35 (
    .D(multiplexer_11_out), .en(and_173_out), .clk(clock_1_out), .Q(register_35_q));  // open: clr
  and and_173 (and_173_out, nor_1_out, and_155_out);
  Register #(.width(32)) register_36 (
    .D(multiplexer_11_out), .en(and_174_out), .clk(clock_1_out), .Q(register_36_q));  // open: clr
  and and_174 (and_174_out, nor_1_out, and_158_out);
  Register #(.width(32)) register_37 (
    .D(multiplexer_11_out), .en(and_175_out), .clk(clock_1_out), .Q(register_37_q));  // open: clr
  and and_175 (and_175_out, nor_1_out, and_161_out);
  Register #(.width(32)) register_38 (
    .D(multiplexer_11_out), .en(and_176_out), .clk(clock_1_out), .Q(register_38_q));  // open: clr
  and and_176 (and_176_out, nor_1_out, and_164_out);
  Register #(.width(32)) register_39 (
    .D(multiplexer_11_out), .en(and_177_out), .clk(clock_1_out), .Q(register_39_q));  // open: clr
  and and_177 (and_177_out, nor_1_out, and_167_out);
  assign bit_extender_62_out = {{31{and_147_out}}, and_147_out};  // Bit_Extender bit_extender_62
  assign bit_extender_63_out = {{31{and_148_out}}, and_148_out};  // Bit_Extender bit_extender_63
  assign bit_extender_64_out = {{31{and_150_out}}, and_150_out};  // Bit_Extender bit_extender_64
  assign bit_extender_65_out = {{31{and_151_out}}, and_151_out};  // Bit_Extender bit_extender_65
  assign bit_extender_66_out = {{31{and_153_out}}, and_153_out};  // Bit_Extender bit_extender_66
  assign bit_extender_67_out = {{31{and_154_out}}, and_154_out};  // Bit_Extender bit_extender_67
  assign bit_extender_68_out = {{31{and_156_out}}, and_156_out};  // Bit_Extender bit_extender_68
  assign bit_extender_69_out = {{31{and_157_out}}, and_157_out};  // Bit_Extender bit_extender_69
  assign bit_extender_70_out = {{31{and_159_out}}, and_159_out};  // Bit_Extender bit_extender_70
  assign bit_extender_71_out = {{31{and_160_out}}, and_160_out};  // Bit_Extender bit_extender_71
  assign bit_extender_72_out = {{31{and_162_out}}, and_162_out};  // Bit_Extender bit_extender_72
  assign bit_extender_73_out = {{31{and_163_out}}, and_163_out};  // Bit_Extender bit_extender_73
  assign bit_extender_74_out = {{31{and_165_out}}, and_165_out};  // Bit_Extender bit_extender_74
  assign bit_extender_75_out = {{31{and_166_out}}, and_166_out};  // Bit_Extender bit_extender_75
  assign bit_extender_76_out = {{31{and_168_out}}, and_168_out};  // Bit_Extender bit_extender_76
  assign bit_extender_77_out = {{31{and_169_out}}, and_169_out};  // Bit_Extender bit_extender_77
  assign or_49_out = and_178_out | or_51_out;  // OR_Gate or_49, 32 bits wide
  assign or_50_out = and_179_out | or_52_out;  // OR_Gate or_50, 32 bits wide
  assign and_178_out = register_32_q & bit_extender_62_out;  // AND_Gate and_178, 32 bits wide
  assign and_179_out = register_32_q & bit_extender_63_out;  // AND_Gate and_179, 32 bits wide
  assign or_51_out = and_180_out | or_53_out;  // OR_Gate or_51, 32 bits wide
  assign or_52_out = and_181_out | or_54_out;  // OR_Gate or_52, 32 bits wide
  assign and_180_out = register_33_q & bit_extender_64_out;  // AND_Gate and_180, 32 bits wide
  assign and_181_out = register_33_q & bit_extender_65_out;  // AND_Gate and_181, 32 bits wide
  assign or_53_out = and_182_out | or_55_out;  // OR_Gate or_53, 32 bits wide
  assign or_54_out = and_183_out | or_56_out;  // OR_Gate or_54, 32 bits wide
  assign and_182_out = register_34_q & bit_extender_66_out;  // AND_Gate and_182, 32 bits wide
  assign and_183_out = register_34_q & bit_extender_67_out;  // AND_Gate and_183, 32 bits wide
  assign or_55_out = and_184_out | or_57_out;  // OR_Gate or_55, 32 bits wide
  assign or_56_out = and_185_out | or_58_out;  // OR_Gate or_56, 32 bits wide
  assign and_184_out = register_35_q & bit_extender_68_out;  // AND_Gate and_184, 32 bits wide
  assign and_185_out = register_35_q & bit_extender_69_out;  // AND_Gate and_185, 32 bits wide
  assign or_57_out = and_186_out | or_59_out;  // OR_Gate or_57, 32 bits wide
  assign or_58_out = and_187_out | or_60_out;  // OR_Gate or_58, 32 bits wide
  assign and_186_out = register_36_q & bit_extender_70_out;  // AND_Gate and_186, 32 bits wide
  assign and_187_out = register_36_q & bit_extender_71_out;  // AND_Gate and_187, 32 bits wide
  assign or_59_out = and_188_out | or_61_out;  // OR_Gate or_59, 32 bits wide
  assign or_60_out = and_189_out | or_62_out;  // OR_Gate or_60, 32 bits wide
  assign and_188_out = register_37_q & bit_extender_72_out;  // AND_Gate and_188, 32 bits wide
  assign and_189_out = register_37_q & bit_extender_73_out;  // AND_Gate and_189, 32 bits wide
  assign or_61_out = and_190_out | and_192_out;  // OR_Gate or_61, 32 bits wide
  assign or_62_out = and_191_out | and_193_out;  // OR_Gate or_62, 32 bits wide
  assign and_190_out = register_38_q & bit_extender_74_out;  // AND_Gate and_190, 32 bits wide
  assign and_191_out = register_38_q & bit_extender_75_out;  // AND_Gate and_191, 32 bits wide
  assign and_192_out = register_39_q & bit_extender_76_out;  // AND_Gate and_192, 32 bits wide
  assign and_193_out = register_39_q & bit_extender_77_out;  // AND_Gate and_193, 32 bits wide
  DotMatrix #(.inputtype("row"), .matrixcols(16), .matrixrows(16)) dotmatrix_1 (
    .row0(register_1_q_2), .row1(register_1_q), .row2(register_3_q_2), .row3(register_3_q),
    .row4(register_5_q_2), .row5(register_5_q), .row6(register_7_q[31:16]), .row7(register_7_q[15:0]),
    .row8(register_2_q_2), .row9(register_2_q), .row10(register_4_q_2), .row11(register_4_q),
    .row12(register_6_q[31:16]), .row13(register_6_q[15:0]), .row14(register_8_q[31:16]),
    .row15(register_8_q[15:0]));

  // Notes on the sheet:
  //   Branch Comp
  //   I/O
  //   Imm Gen
  //   Control Logic
  //   load
  //   ALU_imm
  //   auipc
  //   store
  //   ALU_reg
  //   lui
  //   branch
  //   jalr
  //   jal
  //   ALU
  //   rsA
  //   rsB
  //   Reg File
endmodule

module AND_32bit_Implementation (
  input  [31:0] in_1,
  input  [31:0] in_2,
  output [31:0] out_3
);

  wire [31:0] nand_1_out;

  assign nand_1_out = ~(in_1 & in_2);  // NAND_Gate nand_1, 32 bits wide
  assign out_3 = ~(nand_1_out & nand_1_out);  // NAND_Gate nand_2, 32 bits wide
endmodule

module AND_1bit_Implementation (
  input  in_1,
  input  in_2,
  output out_3
);

  wire nand_2_out;

  nand nand_1 (out_3, nand_2_out, nand_2_out);
  nand nand_2 (nand_2_out, in_1, in_2);
endmodule

module AND_24bit_implementation (
  input  [23:0] in_1,
  input  [23:0] in_2,
  output out_3
);

  wire [23:0] nand_1_out;
  wire [23:1] nand_2_out;

  assign nand_1_out = ~(in_1 & in_2);  // NAND_Gate nand_1, 24 bits wide
  assign {nand_2_out, out_3} = ~(nand_1_out & nand_1_out);  // NAND_Gate nand_2, 24 bits wide
  // Pins of 1 and 24 bits meet at {nand_2_out, out_3}
endmodule

module OR_2Input_Implementation (
  input  in_1,
  input  in_2,
  output out_3
);

  wire nand_1_out, nand_2_out;

  nand nand_1 (nand_1_out, in_1, in_1);
  nand nand_2 (nand_2_out, in_2, in_2);
  nand nand_3 (out_3, nand_1_out, nand_2_out);
endmodule

module OR_32bit_2Input_Implementation (
  input  [31:0] in_1,
  input  [31:0] in_2,
  output [31:0] out_3
);

  wire [31:0] nand_1_out, nand_2_out;

  assign nand_1_out = ~(in_1 & in_1);  // NAND_Gate nand_1, 32 bits wide
  assign nand_2_out = ~(in_2 & in_2);  // NAND_Gate nand_2, 32 bits wide
  assign out_3 = ~(nand_1_out & nand_2_out);  // NAND_Gate nand_3, 32 bits wide
endmodule

module OR_1bit_3Input_Implementation (
  input  in_1,
  input  in_2,
  input  in_3,
  output out_4
);

  wire nand_1_out, nand_2_out, nand_3_out;

  nand nand_1 (nand_1_out, in_1, in_1);
  nand nand_2 (nand_2_out, in_2, in_2);
  nand nand_3 (nand_3_out, in_3, in_3);
  nand nand_4 (out_4, nand_1_out, nand_2_out, nand_3_out);
endmodule

module OR_32bit_5Input_implementation (
  input  [31:0] in_1,
  input  [31:0] in_2,
  input  [31:0] in_3,
  input  [31:0] in_4,
  input  [31:0] in_5,
  output [31:0] out_6
);

  wire [31:0] nand_1_out, nand_2_out, nand_3_out, nand_4_out, nand_5_out;

  assign nand_1_out = ~(in_1 & in_1);  // NAND_Gate nand_1, 32 bits wide
  assign nand_2_out = ~(in_2 & in_2);  // NAND_Gate nand_2, 32 bits wide
  assign nand_3_out = ~(in_3 & in_3);  // NAND_Gate nand_3, 32 bits wide
  assign nand_4_out = ~(in_4 & in_4);  // NAND_Gate nand_4, 32 bits wide
  assign nand_5_out = ~(in_5 & in_5);  // NAND_Gate nand_5, 32 bits wide
  assign out_6 = ~(nand_1_out & nand_2_out & nand_3_out & nand_4_out & nand_5_out);  // NAND_Gate nand_6, 32 bits wide
endmodule

module XOR_1bit_2Input_Implementation (
  input  in_1,
  input  in_2,
  output out_3
);

  wire nand_1_out, nand_2_out, nand_3_out;

  nand nand_1 (nand_1_out, in_1, in_2);
  nand nand_2 (nand_2_out, in_1, nand_1_out);
  nand nand_3 (nand_3_out, nand_1_out, in_2);
  nand nand_4 (out_3, nand_2_out, nand_3_out);
endmodule

module XOR_32bit_2Input_Implementation (
  input  [31:0] in_1,
  input  [31:0] in_2,
  output [31:0] out_3
);

  wire [31:0] nand_1_out, nand_2_out, nand_3_out;

  assign nand_1_out = ~(in_1 & in_2);  // NAND_Gate nand_1, 32 bits wide
  assign nand_2_out = ~(in_1 & nand_1_out);  // NAND_Gate nand_2, 32 bits wide
  assign nand_3_out = ~(nand_1_out & in_2);  // NAND_Gate nand_3, 32 bits wide
  assign out_3 = ~(nand_2_out & nand_3_out);  // NAND_Gate nand_4, 32 bits wide
endmodule
